// Logisim project brainfuck.circ as structural Verilog: 3 circuits, main circuit main
module main (
  input  using_rom
);

  wire and_1_out, brainfuck_cpu_1_err, brainfuck_cpu_1_stdin_read, brainfuck_cpu_1_stdin_waiting,
       brainfuck_cpu_1_stdout_ready, brainfuck_cpu_1_writing_mem, clk, clock_1_out, clr_2_out, clr_out,
       comparator_1_eq, d_ff_1_q, d_ff_2_q, d_ff_3_q, d_ff_3_qn, d_ff_4_q, or_1_out;
  wire [3:0] rom_1_data;
  wire [5:0] brainfuck_cpu_1_dbg_skip_stack_size, brainfuck_cpu_1_dbg_stack_length;
  wire [6:0] bit_extender_2_out, keyboard_1_data;
  wire [7:0] bit_extender_1_out, brainfuck_cpu_1_set_mem, brainfuck_cpu_1_stdout, multiplexer_1_out,
       multiplexer_2_out, multiplexer_3_out, ram_1_data, register_3_q, register_4_q, rom_2_data;
  wire [8:8] keyboard_1_avail, multiplexer_2_out_2;
  wire [23:0] brainfuck_cpu_1_instr_ptr_2, brainfuck_cpu_1_mem_ptr_2, counter_1_q, counter_3_q, register_1_q,
       register_2_q;
  wire [31:0] counter_2_q;

  Keyboard #(.buflen(256)) keyboard_1 (
    .clk(clk), .re(d_ff_2_q), .clr(clr_out), .avail(keyboard_1_avail[8]), .data(keyboard_1_data));
  Button clr (.out(clr_out));
  LED Pending_input (.in(brainfuck_cpu_1_stdin_waiting));
  and and_1 (and_1_out, using_rom, clk);
  and and_2 (clk, clock_1_out, ~or_1_out);  // AND_Gate
  Clock clock_1 (.out(clock_1_out));
  D_Flip_Flop d_ff_1 (.clk(clock_1_out), .D(or_1_out), .Q(d_ff_1_q));  // open: Qn, preset, en, reset
  Counter #(.width(24), .max('hffffff)) counter_1 (
    .count(d_ff_2_q), .Q(counter_1_q), .clk(and_1_out));  // open: load, D, carry, clr
  or or_1 (or_1_out, d_ff_1_q, rom_1_data[3]);
  ROM #(.addrWidth(24), .dataWidth(4)) rom_1 (.addr(register_1_q), .data(rom_1_data));  // open: sel
  LED Program_complete (.in(or_1_out));
  assign bit_extender_1_out = {{1{1'b0}}, keyboard_1_data};  // Bit_Extender bit_extender_1
  Multiplexer #(.width(8), .enable("false")) multiplexer_1 (
    .in0(bit_extender_1_out), .in1({8{1'b0}}), .out(multiplexer_1_out), .sel(comparator_1_eq));
  Comparator #(.width(7)) comparator_1 (.a(keyboard_1_data), .b(7'b0001100), .eq(comparator_1_eq));  // open: gt, lt
  ROM #(.addrWidth(24)) rom_2 (.addr(counter_1_q), .data(rom_2_data));  // open: sel
  // Probe on counter_2_q
  Counter #(.width(32), .max('hffffffff)) counter_2 (
    .count(1'b1), .Q(counter_2_q), .clk(clk));  // open: load, D, carry, clr
  // Probe on brainfuck_cpu_1_instr_ptr_2
  // Probe on brainfuck_cpu_1_dbg_skip_stack_size
  LED led_1 (.in(brainfuck_cpu_1_err));
  Multiplexer #(.width(9), .enable("false")) multiplexer_2 (
    .in0({keyboard_1_avail[8], multiplexer_1_out}), .in1({1'b1, rom_2_data}),
    .out({multiplexer_2_out_2[8], multiplexer_2_out}), .sel(using_rom));
  // Probe on brainfuck_cpu_1_writing_mem
  // Probe on brainfuck_cpu_1_mem_ptr_2
  // Probe on brainfuck_cpu_1_dbg_stack_length
  brainfuck_cpu brainfuck_cpu_1 (
    .instr(rom_1_data[2:0]), .instr_ptr(register_1_q), .mem(multiplexer_3_out), .mem_ptr(register_2_q),
    .stdin(multiplexer_2_out), .instr_ptr_2(brainfuck_cpu_1_instr_ptr_2),
    .mem_ptr_2(brainfuck_cpu_1_mem_ptr_2), .writing_mem(brainfuck_cpu_1_writing_mem),
    .set_mem(brainfuck_cpu_1_set_mem), .stdout_ready(brainfuck_cpu_1_stdout_ready),
    .stdout(brainfuck_cpu_1_stdout), .stdin_read(brainfuck_cpu_1_stdin_read), .clk(clk),
    .err(brainfuck_cpu_1_err), .dbg_stack_length(brainfuck_cpu_1_dbg_stack_length),
    .dbg_skip_stack_size(brainfuck_cpu_1_dbg_skip_stack_size), .stdin_ready(multiplexer_2_out_2[8]),
    .stdin_waiting(brainfuck_cpu_1_stdin_waiting));
  // Probe on brainfuck_cpu_1_stdout_ready
  // Probe on brainfuck_cpu_1_set_mem
  // Probe on brainfuck_cpu_1_stdout
  Register #(.width(24)) register_1 (.D(brainfuck_cpu_1_instr_ptr_2), .Q(register_1_q), .clk(clk));  // open: en, clr
  D_Flip_Flop d_ff_2 (.clk(clk), .D(brainfuck_cpu_1_stdin_read), .Q(d_ff_2_q));  // open: Qn, preset, en, reset
  // Probe on brainfuck_cpu_1_stdin_read
  Register #(.width(24)) register_2 (.D(brainfuck_cpu_1_mem_ptr_2), .Q(register_2_q), .clk(clk));  // open: en, clr
  D_Flip_Flop d_ff_3 (
    .clk(clk), .D(brainfuck_cpu_1_writing_mem), .Q(d_ff_3_q), .Qn(d_ff_3_qn));  // open: preset, en, reset
  Register register_3 (.D(brainfuck_cpu_1_set_mem), .Q(register_3_q), .clk(clk));  // open: en, clr
  D_Flip_Flop d_ff_4 (.clk(clk), .D(brainfuck_cpu_1_stdout_ready), .Q(d_ff_4_q));  // open: Qn, preset, en, reset
  Register register_4 (.D(brainfuck_cpu_1_stdout), .Q(register_4_q), .clk(clk));  // open: en, clr
  // Probe on multiplexer_3_out
  Multiplexer #(.width(8), .enable("false")) multiplexer_3 (
    .in0(register_3_q), .in1(ram_1_data), .out(multiplexer_3_out), .sel(d_ff_3_qn));
  Button clr_2 (.out(clr_2_out));
  Bit_Extender #(.out_width(7), .\type ("sign")) bit_extender_2 (.in(register_4_q), .out(bit_extender_2_out));
  TTY tty_1 (.data(bit_extender_2_out), .clk(clk), .we(d_ff_4_q), .clr(clr_2_out));
  RAM #(.addrWidth(24), .bus("separate")) ram_1 (
    .addr(register_2_q), .din(register_3_q), .data(ram_1_data), .str(d_ff_3_q), .clk(clk), .ld(1'b1));  // open: sel, clr
  Counter #(.width(24), .max('hffffff)) counter_3 (
    .count(d_ff_4_q), .Q(counter_3_q), .clk(clk));  // open: load, D, carry, clr
  RAM #(.addrWidth(24), .bus("separate")) ram_2 (
    .addr(counter_3_q), .din(register_4_q), .str(d_ff_4_q), .clk(clk));  // open: data, sel, ld, clr

  // Notes on the sheet:
  //   contents of rom_1 (hex, n*v repeats v):
  //   2 6 0 5 0 2 1 6 4 0 3 7 0 6 1 1 3 0 0 3 0 7 1 1 1 7 8
  //   contents of rom_2 (hex, n*v repeats v):
  //   d3 ad be 3f ca fe f3 3d
endmodule

// BF\nCPU
module brainfuck_cpu (
  input  [2:0] instr,
  input  [23:0] instr_ptr,
  input  [7:0] mem,
  input  clk,
  input  [23:0] mem_ptr,
  input  stdin_ready,
  input  [7:0] stdin,
  output [23:0] instr_ptr_2,
  output [23:0] mem_ptr_2,
  output writing_mem,
  output [7:0] set_mem,
  output stdout_ready,
  output [7:0] stdout,
  output stdin_read,
  output stdin_waiting,
  output err,
  output [5:0] dbg_stack_length,
  output [5:0] dbg_skip_stack_size
);

  wire and_1_out, and_2_out, and_3_out, and_4_out, and_5_out, and_7_out, and_8_out, comparator_1_eq,
       err_stack, \input , input_minus, input_plus, input_t_t, input_t_t_t, input_t_t_t_t, input_t_t_t_t_t,
       mem____0_out, nand_1_out, or_1_out, or_2_out, or_3_out;
  wire [5:0] adder_1_out, bit_extender_1_out;
  wire [7:0] adder_4_out, bit_extender_3_out;
  wire [23:0] bit_extender_2_out, multiplexer_1_out, register24stack64_1_tail;

  and and_1 (and_1_out, instr[2], instr[1]);
  and and_2 (and_2_out, input_t_t_t_t, mem____0_out);
  and and_3 (and_3_out, ~mem____0_out, ~or_3_out, input_t_t_t_t_t);  // AND_Gate
  and and_4 (and_4_out, or_3_out, input_t_t_t_t_t);
  assign bit_extender_1_out = {{5{and_4_out}}, and_4_out};  // Bit_Extender bit_extender_1
  Demultiplexer #(.select(3)) demultiplexer_1 (
    .out0(input_t_t_t), .out1(input_t_t), .out2(input_plus), .out3(input_minus), .out4(stdout_ready),
    .out5(\input ), .out6(input_t_t_t_t), .out7(input_t_t_t_t_t), .in(or_1_out), .sel(instr));  // open: en
  or or_1 (or_1_out, ~or_3_out, and_1_out);  // OR_Gate
  Register24Stack64 register24stack64_1 (
    .clk(clk), .push(and_2_out), .insert_data(instr_ptr), .pop(and_3_out), .tail(register24stack64_1_tail),
    .err(err_stack), .length(dbg_stack_length));
  or or_2 (or_2_out, ~mem____0_out, or_3_out);  // OR_Gate
  and and_5 (and_5_out, or_2_out, input_t_t_t_t);
  Adder #(.width(6)) adder_1 (
    .a(bit_extender_1_out), .b(dbg_skip_stack_size), .out(adder_1_out), .cin(and_5_out));  // open: cout
  or or_3 (or_3_out, dbg_skip_stack_size[5], dbg_skip_stack_size[4], dbg_skip_stack_size[3], dbg_skip_stack_size[2], dbg_skip_stack_size[1], dbg_skip_stack_size[0]);
  Register #(.width(6)) register_1 (.D(adder_1_out), .Q(dbg_skip_stack_size), .clk(clk));  // open: en, clr
  or mem____0 (mem____0_out, mem[7], mem[6], mem[5], mem[4], mem[3], mem[2], mem[1], mem[0]);
  and and_6 (stdin_read, \input , stdin_ready);
  // Probe on dbg_stack_length
  Comparator #(.width(6)) comparator_1 (.a(dbg_stack_length), .b({6{1'b0}}), .eq(comparator_1_eq));  // open: gt, lt
  and and_7 (and_7_out, comparator_1_eq, input_t_t_t_t_t);
  Multiplexer #(.width(24)) multiplexer_1 (
    .in0(instr_ptr), .in1(register24stack64_1_tail), .out(multiplexer_1_out), .sel(and_8_out));  // open: en
  and and_8 (and_8_out, input_t_t_t_t_t, mem____0_out);
  and and_9 (stdin_waiting, \input , ~stdin_ready);  // AND_Gate
  or or_4 (err, err_stack, and_7_out);
  assign bit_extender_2_out = {{23{input_t_t}}, input_t_t};  // Bit_Extender bit_extender_2
  assign bit_extender_3_out = {{7{input_minus}}, input_minus};  // Bit_Extender bit_extender_3
  nand nand_1 (nand_1_out, ~stdin_ready, \input );  // NAND_Gate
  Adder #(.width(24)) adder_2 (
    .a(multiplexer_1_out), .b({24{1'b0}}), .out(instr_ptr_2), .cin(nand_1_out));  // open: cout
  Adder #(.width(24)) adder_3 (.a(mem_ptr), .b(bit_extender_2_out), .out(mem_ptr_2), .cin(input_t_t_t));  // open: cout
  or or_5 (writing_mem, input_plus, input_minus, stdin_read);
  Adder adder_4 (.a(mem), .b(bit_extender_3_out), .out(adder_4_out), .cin(input_plus));  // open: cout
  Multiplexer #(.width(8)) multiplexer_2 (.in0(adder_4_out), .in1(stdin), .out(set_mem), .sel(stdin_read));  // open: en

  assign stdout = mem;

  // Other names for the same wires on the sheet: input_t = stdout_ready; stack_length[5:0] = dbg_stack_length
endmodule

// Register24\nStack[64]
module Register24Stack64 (
  input  clk,
  input  push,
  input  pop,
  input  [23:0] insert_data,
  output [5:0] length,
  output [23:0] tail,
  output err
);

  wire and_1_out, and_2_out, and_3_out, comparator_1_eq, comparator_2_eq, not_1_out, not_2_out, not_3_out,
       or_1_out;
  wire [5:0] adder_1_out, bit_extender_1_out, subtractor_1_out;
  wire [23:0] multiplexer_1_out;

  not not_1 (not_1_out, push);
  Subtractor #(.width(6)) subtractor_1 (
    .a(length), .b({6{1'b0}}), .out(subtractor_1_out), .bin(not_1_out));  // open: bout
  Multiplexer #(.width(24), .enable("false")) multiplexer_1 (
    .in0({24{1'b0}}), .in1(insert_data), .out(multiplexer_1_out), .sel(push));
  assign bit_extender_1_out = {{5{pop}}, pop};  // Bit_Extender bit_extender_1
  not not_2 (not_2_out, err);
  not not_3 (not_3_out, or_1_out);
  or or_1 (or_1_out, push, pop);
  Adder #(.width(6)) adder_1 (.a(length), .b(bit_extender_1_out), .out(adder_1_out), .cin(push));  // open: cout
  Register #(.width(6)) u_length (.D(adder_1_out), .Q(length), .clk(clk));  // open: en, clr
  RAM #(.addrWidth(6), .dataWidth(24), .bus("separate")) ram_1 (
    .addr(subtractor_1_out), .din(multiplexer_1_out), .data(tail), .str(or_1_out), .sel(not_2_out),
    .clk(clk), .ld(not_3_out));  // open: clr
  Comparator #(.width(6)) comparator_1 (.a({6{1'b1}}), .b(length), .eq(comparator_1_eq));  // open: gt, lt
  Comparator #(.width(6)) comparator_2 (.a({6{1'b0}}), .b(length), .eq(comparator_2_eq));  // open: gt, lt
  and and_1 (and_1_out, comparator_1_eq, push);
  and and_2 (and_2_out, push, pop);
  and and_3 (and_3_out, comparator_2_eq, pop);
  or or_2 (err, and_1_out, and_2_out, and_3_out);
endmodule
